# Fritzing sketch SistemaRiego (saved by Fritzing 0.9.3b)

parts:
  Componente1 = Arduino Uno (Rev3)
  R1 = Resistor [tolerance=±5% resistance=220 package=THT]
  J1 = Piezo Speaker
  R2 = Resistor [tolerance=±5% resistance=220 package=THT]
  R3 = Resistor [tolerance=±5% resistance=220 package=THT]
  Componente2 = Soil Moisture Sensor
  M1 = DC Motor

nets:
  N1: Componente1.A0, Componente2.SIG
  N2: Componente1.D9_PWM, J1.pin2
  N3: Componente1.GND, R1.Pin_1, R2.Pin_0, R3.Pin_0
  N4: Componente1.D6_PWM, M1.pin_2
  N5: R3.Pin_1, Componente2.GND
